// Logisim project control-logic.circ as structural Verilog: 14 circuits, main circuit control_logic
module control_logic (
  input  [31:0] inst,
  input  BrEq,
  input  BrLt,
  output [3:0] write_enable,
  output out_5,
  output RegWEn,
  output [2:0] ImmSel,
  output BrUn,
  output ASel,
  output BSel,
  output [3:0] ALUSel,
  output MemRW,
  output [1:0] WBSel,
  output CSRSel,
  output CSRWen
);

  wire [2:0] funct3;
  wire [3:0] InstructionIndex;
  wire [6:0] funct7;

  // Probe on funct3
  // Probe on funct7
  // Probe on InstructionIndex
  InstructionDecode instructiondecode_1 (.inst(inst), .InstructionIndex(InstructionIndex));
  funct funct_1 (.inst(inst), .funct3(funct3), .funct7(funct7));
  Br_Un br_un_1 (.funct3(funct3), .BrUn(BrUn));
  ImmS imms_1 (.Inst_Index(InstructionIndex), .ImmSel(ImmSel));
  ALUS alus_1 (.Inst_Index(InstructionIndex), .funct7(funct7), .funct3(funct3), .ALUSel(ALUSel));
  Mem_RW mem_rw_1 (.Inst_Index(InstructionIndex), .MemRW(MemRW));
  WBS wbs_1 (.Inst_Index(InstructionIndex), .PCSel(out_5), .WBSel(WBSel));
  PCS pcs_1 (.Inst_Index(InstructionIndex), .funct3(funct3), .BrEq(BrEq), .BrLt(BrLt), .PC_Sel(out_5));
  RegW regw_1 (.inst_index(InstructionIndex), .RegWen(RegWEn));
  BS bs_1 (.inst_index(InstructionIndex), .BSel(BSel));
  AS as_1 (.inst_index(InstructionIndex), .ASel(ASel));
  CSR csr_1 (.Inst_Index(InstructionIndex), .fuct3(funct3), .CSRSel(CSRSel), .CSRWen(CSRWen));
  writeEnable writeenable_1 (.Inst_Index(InstructionIndex), .funct3(funct3), .write_enable(write_enable));

  // Other names for the same wires on the sheet: PCSel = out_5

  // Notes on the sheet:
  //   INPUTS to your circuit
  //   DON'T CHANGE THE LOCATIONS OF THE INPUTS AND OUTPUTS!
  //   OUTPUT from your circuit
  //   Custom output
endmodule

module InstructionDecode (
  input  [31:0] inst,
  output [3:0] InstructionIndex
);

  wire B, BJJALR, CSR, I1, I2, IU, J, JALR, R, R_U2, S, U1, U2;

  Demultiplexer #(.enable("false"), .select(3)) demultiplexer_1 (
    .out0(I1), .out1(IU), .out2(S), .out3(R_U2), .out6(BJJALR), .out7(CSR), .in(1'b1), .sel(inst[6:4]));  // open: out4, out5
  Priority_Encoder #(.select(4)) priority_encoder_1 (
    .in0(R), .in1(I1), .in2(I2), .in3(S), .in4(B), .in5(U1), .in6(J), .in7(JALR), .in8(CSR), .in9(U2),
    .out(InstructionIndex));  // open: in10, in11, in12, in13, in14, in15, gs, en_out, en_in
  Demultiplexer #(.enable("false"), .select(4)) demultiplexer_2 (
    .out3(I2), .out7(U1), .in(IU), .sel(inst[3:0]));  // open: out0, out1, out2, out4, out5, out6, out8, out9, out10, out11, out12, out13, out14, out15
  Demultiplexer #(.enable("false"), .select(4)) demultiplexer_3 (
    .out3(R), .out7(U2), .in(R_U2), .sel(inst[3:0]));  // open: out0, out1, out2, out4, out5, out6, out8, out9, out10, out11, out12, out13, out14, out15
  Demultiplexer #(.enable("false"), .select(4)) demultiplexer_4 (
    .out3(B), .out7(JALR), .out15(J), .in(BJJALR), .sel(inst[3:0]));  // open: out0, out1, out2, out4, out5, out6, out8, out9, out10, out11, out12, out13, out14
endmodule

module PCS (
  input  [3:0] Inst_Index,
  input  [2:0] funct3,
  input  BrEq,
  input  BrLt,
  output PC_Sel
);

  wire demultiplexer_1_out0, demultiplexer_1_out1, demultiplexer_1_out4, demultiplexer_1_out5,
       demultiplexer_1_out6, demultiplexer_1_out7, or_1_out, PCSel_B, PCSel_eq, PCSel_lt, PCSel_lt_u;

  Demultiplexer #(.enable("false"), .select(3)) demultiplexer_1 (
    .out0(demultiplexer_1_out0), .out1(demultiplexer_1_out1), .out4(demultiplexer_1_out4),
    .out5(demultiplexer_1_out5), .out6(demultiplexer_1_out6), .out7(demultiplexer_1_out7), .in(1'b1),
    .sel(funct3));  // open: out2, out3
  Multiplexer #(.enable("false")) multiplexer_1 (
    .in0(demultiplexer_1_out1), .in1(demultiplexer_1_out0), .out(PCSel_eq), .sel(BrEq));
  Multiplexer #(.enable("false")) multiplexer_2 (
    .in0(demultiplexer_1_out5), .in1(demultiplexer_1_out4), .out(PCSel_lt), .sel(BrLt));
  Multiplexer #(.enable("false")) multiplexer_3 (
    .in0(demultiplexer_1_out7), .in1(demultiplexer_1_out6), .out(PCSel_lt_u), .sel(BrLt));
  or or_1 (or_1_out, PCSel_eq, PCSel_lt);
  or or_2 (PCSel_B, or_1_out, PCSel_lt_u);
  Multiplexer #(.enable("false"), .select(4)) multiplexer_4 (
    .in0(1'b0), .in1(1'b0), .in2(1'b0), .in3(1'b0), .in4(PCSel_B), .in5(1'b0), .in6(1'b1), .in7(1'b1),
    .in8(1'b0), .in9(1'b0), .out(PC_Sel), .sel(Inst_Index));  // open: in10, in11, in12, in13, in14, in15

  // Other names for the same wires on the sheet: InstructionIndex[3:0] = Inst_Index; PCSel = PC_Sel
endmodule

module funct (
  input  [31:0] inst,
  output [2:0] funct3,
  output [6:0] funct7
);


  assign funct3 = inst[14:12];
  assign funct7 = inst[31:25];
endmodule

module RegW (
  input  [3:0] inst_index,
  output RegWen
);

  Multiplexer #(.enable("false"), .select(4)) multiplexer_1 (
    .in0(1'b1), .in1(1'b1), .in2(1'b1), .in3(1'b0), .in4(1'b0), .in5(1'b1), .in6(1'b1), .in7(1'b1),
    .in9(1'b1), .out(RegWen), .sel(inst_index));  // open: in8, in10, in11, in12, in13, in14, in15

  // Other names for the same wires on the sheet: InstructionIndex[3:0] = inst_index
endmodule

module BS (
  input  [3:0] inst_index,
  output BSel
);

  Multiplexer #(.enable("false"), .select(4)) multiplexer_1 (
    .in0(1'b0), .in1(1'b1), .in2(1'b1), .in3(1'b1), .in4(1'b1), .in5(1'b1), .in6(1'b1), .in7(1'b1),
    .in9(1'b1), .out(BSel), .sel(inst_index));  // open: in8, in10, in11, in12, in13, in14, in15

  // Other names for the same wires on the sheet: InstructionIndex[3:0] = inst_index
endmodule

module AS (
  input  [3:0] inst_index,
  output ASel
);

  Multiplexer #(.enable("false"), .select(4)) multiplexer_1 (
    .in0(1'b0), .in1(1'b0), .in2(1'b0), .in3(1'b0), .in4(1'b1), .in5(1'b1), .in6(1'b1), .in7(1'b0),
    .out(ASel), .sel(inst_index));  // open: in8, in9, in10, in11, in12, in13, in14, in15

  // Other names for the same wires on the sheet: InstructionIndex[3:0] = inst_index
endmodule

module Br_Un (
  input  [2:0] funct3,
  output BrUn
);

  wire demultiplexer_1_out6, demultiplexer_1_out7;

  Demultiplexer #(.enable("false"), .select(3)) demultiplexer_1 (
    .out6(demultiplexer_1_out6), .out7(demultiplexer_1_out7), .in(1'b1), .sel(funct3));  // open: out0, out1, out2, out3, out4, out5
  or or_1 (BrUn, demultiplexer_1_out6, demultiplexer_1_out7);
endmodule

module ALUS (
  input  [3:0] Inst_Index,
  input  [6:0] funct7,
  input  [2:0] funct3,
  output [3:0] ALUSel
);

  wire demultiplexer_3_out0, is_add_i2, is_add_r, is_and_i2, is_and_r, is_and_sub_mul_r, is_mul_r, is_mulh_r,
       is_mulhu_r, is_or_i2, is_or_r, is_sll_i2, is_sll_mulh_r, is_sll_r, is_slt_i2, is_slt_r, is_sra_i2,
       is_sra_r, is_srl_i2, is_srl_r, is_srl_sra_i2, is_srl_sra_r, is_sub_r, is_xor_i2, is_xor_r;
  wire [3:0] ALU_i2, ALU_R;

  Demultiplexer #(.enable("false"), .select(3)) demultiplexer_1 (
    .out0(is_and_sub_mul_r), .out1(is_sll_mulh_r), .out2(is_slt_r), .out3(is_mulhu_r), .out4(is_xor_r),
    .out5(is_srl_sra_r), .out6(is_or_r), .out7(is_and_r), .in(1'b1), .sel(funct3));
  Demultiplexer #(.enable("false"), .select(3)) demultiplexer_2 (
    .out0(is_add_i2), .out1(is_sll_i2), .out2(is_slt_i2), .out4(is_xor_i2), .out5(is_srl_sra_i2),
    .out6(is_or_i2), .out7(is_and_i2), .in(1'b1), .sel(funct3));  // open: out3
  Demultiplexer #(.enable("false")) demultiplexer_3 (
    .out0(demultiplexer_3_out0), .out1(is_sub_r), .in(is_and_sub_mul_r), .sel(funct7[6]));
  Demultiplexer #(.enable("false")) demultiplexer_4 (
    .out0(is_sll_r), .out1(is_mulh_r), .in(is_sll_mulh_r), .sel(funct7[0]));
  Demultiplexer #(.enable("false")) demultiplexer_5 (
    .out0(is_srl_r), .out1(is_sra_r), .in(is_srl_sra_r), .sel(funct7[6]));
  Demultiplexer #(.enable("false")) demultiplexer_6 (
    .out0(is_srl_i2), .out1(is_sra_i2), .in(is_srl_sra_i2), .sel(funct7[6]));
  Demultiplexer #(.enable("false")) demultiplexer_7 (
    .out0(is_add_r), .out1(is_mul_r), .in(demultiplexer_3_out0), .sel(funct7[0]));
  Multiplexer #(.enable("false"), .select(4), .width(4)) multiplexer_1 (
    .in0(ALU_R), .in1(4'b0000), .in2(ALU_i2), .in3(4'b0000), .in4(4'b0000), .in5(4'b0000), .in6(4'b0000),
    .in7(4'b0000), .in9(4'b1111), .out(ALUSel), .sel(Inst_Index));  // open: in8, in10, in11, in12, in13, in14, in15
  Priority_Encoder #(.select(4)) priority_encoder_1 (
    .in0(is_add_i2), .in1(is_sll_i2), .in2(is_slt_i2), .in4(is_xor_i2), .in5(is_srl_i2), .in6(is_or_i2),
    .in7(is_and_i2), .in13(is_sra_i2), .out(ALU_i2));  // open: in3, in8, in9, in10, in11, in12, in14, in15, gs, en_out, en_in
  Priority_Encoder #(.select(4)) priority_encoder_2 (
    .in0(is_add_r), .in1(is_sll_r), .in2(is_slt_r), .in4(is_xor_r), .in5(is_srl_r), .in6(is_or_r),
    .in7(is_and_r), .in8(is_mul_r), .in9(is_mulh_r), .in11(is_mulhu_r), .in12(is_sub_r), .in13(is_sra_r),
    .out(ALU_R));  // open: in3, in10, in14, in15, gs, en_out, en_in
endmodule

module ImmS (
  input  [3:0] Inst_Index,
  output [2:0] ImmSel
);

  Multiplexer #(.enable("false"), .select(4), .width(3)) multiplexer_1 (
    .in1(3'b011), .in2(3'b011), .in3(3'b100), .in4(3'b101), .in5(3'b110), .in6(3'b111), .in7(3'b011),
    .in9(3'b110), .out(ImmSel), .sel(Inst_Index));  // open: in0, in8, in10, in11, in12, in13, in14, in15

  // Other names for the same wires on the sheet: InstructionIndex[3:0] = Inst_Index
endmodule

module Mem_RW (
  input  [3:0] Inst_Index,
  output MemRW
);

  Multiplexer #(.enable("false"), .select(4)) multiplexer_1 (
    .in0(1'b0), .in1(1'b0), .in2(1'b0), .in3(1'b1), .in4(1'b0), .in5(1'b0), .in6(1'b0), .in7(1'b0),
    .in9(1'b0), .out(MemRW), .sel(Inst_Index));  // open: in8, in10, in11, in12, in13, in14, in15
endmodule

module WBS (
  input  [3:0] Inst_Index,
  input  PCSel,
  output [1:0] WBSel
);

  wire [1:0] WBSel_B;

  Multiplexer #(.enable("false"), .width(2)) multiplexer_1 (.in1(2'b10), .out(WBSel_B), .sel(PCSel));  // open: in0
  Multiplexer #(.enable("false"), .select(4), .width(2)) multiplexer_2 (
    .in0(2'b01), .in1(2'b00), .in2(2'b01), .in4(WBSel_B), .in5(2'b01), .in6(2'b10), .in7(2'b10), .in9(2'b01),
    .out(WBSel), .sel(Inst_Index));  // open: in3, in8, in10, in11, in12, in13, in14, in15
endmodule

module CSR (
  input  [3:0] Inst_Index,
  input  [2:0] fuct3,
  output CSRSel,
  output CSRWen
);

  wire multiplexer_1_out;

  Multiplexer #(.enable("false"), .select(4)) multiplexer_1 (
    .in0(1'b0), .in1(1'b0), .in2(1'b0), .in3(1'b0), .in4(1'b0), .in5(1'b0), .in6(1'b0), .in7(1'b0),
    .in8(1'b1), .in9(1'b0), .out(multiplexer_1_out), .sel(Inst_Index));  // open: in10, in11, in12, in13, in14, in15
  Multiplexer #(.enable("false")) multiplexer_2 (.in0(1'b0), .in1(multiplexer_1_out), .out(CSRSel), .sel(fuct3[2]));
  Multiplexer #(.enable("false"), .select(4)) multiplexer_3 (
    .in0(1'b0), .in1(1'b0), .in2(1'b0), .in3(1'b0), .in4(1'b0), .in5(1'b0), .in6(1'b0), .in7(1'b0),
    .in8(1'b1), .in9(1'b0), .out(CSRWen), .sel(Inst_Index));  // open: in10, in11, in12, in13, in14, in15

  // Other names for the same wires on the sheet: funct3[2:0] = fuct3; InstructionIndex[3:0] = Inst_Index
endmodule

module writeEnable (
  input  [3:0] Inst_Index,
  input  [2:0] funct3,
  output [3:0] write_enable
);

  wire [3:0] write_enable_b, write_enable_h, write_enable_w;

  Demultiplexer #(.enable("false"), .select(4), .width(4)) demultiplexer_1 (
    .out3(write_enable_b), .in(4'b0001), .sel(Inst_Index));  // open: out0, out1, out2, out4, out5, out6, out7, out8, out9, out10, out11, out12, out13, out14, out15
  Demultiplexer #(.enable("false"), .select(4), .width(4)) demultiplexer_2 (
    .out3(write_enable_h), .in(4'b0011), .sel(Inst_Index));  // open: out0, out1, out2, out4, out5, out6, out7, out8, out9, out10, out11, out12, out13, out14, out15
  Demultiplexer #(.enable("false"), .select(4), .width(4)) demultiplexer_3 (
    .out3(write_enable_w), .in(4'b1111), .sel(Inst_Index));  // open: out0, out1, out2, out4, out5, out6, out7, out8, out9, out10, out11, out12, out13, out14, out15
  Multiplexer #(.enable("false"), .select(3), .width(4)) multiplexer_1 (
    .in0(write_enable_b), .in1(write_enable_h), .in2(write_enable_w), .out(write_enable), .sel(funct3));  // open: in3, in4, in5, in6, in7
endmodule
