// Logisim project imm-gen.circ as structural Verilog: 1 circuit, main circuit imm_gen
module imm_gen (
  input  [31:0] inst,
  input  [2:0] ImmSel,
  output [31:0] imm
);

  wire [31:0] adder_2_out, adder_3_out, adder_4_out, adder_5_out, adder_7_out, B, bit_extender_2_out,
       bit_extender_3_out, bit_extender_4_out, bit_extender_5_out, bit_extender_6_out, bit_extender_7_out,
       bit_extender_8_out, bit_extender_9_out, bit_extender_10_out, bit_extender_11_out, bit_extender_12_out,
       bit_extender_13_out, I, S, shifter_1_out, shifter_2_out, shifter_3_out, shifter_5_out, shifter_6_out,
       shifter_7_out, shifter_8_out, shifter_9_out, shifter_10_out, shifter_11_out, U, UJ;

  // Probe on bit_extender_6_out
  // Probe on shifter_5_out
  assign I = {{20{inst[31]}}, inst[31:20]};  // Bit_Extender bit_extender_1
  assign bit_extender_2_out = {{25{inst[31]}}, inst[31:25]};  // Bit_Extender bit_extender_2
  assign bit_extender_3_out = {{27{1'b0}}, inst[11:7]};  // Bit_Extender bit_extender_3
  assign bit_extender_4_out = {{31{inst[31]}}, inst[31]};  // Bit_Extender bit_extender_4
  assign bit_extender_5_out = {{31{1'b0}}, inst[7]};  // Bit_Extender bit_extender_5
  assign bit_extender_6_out = {{12{1'b0}}, inst[31:12]};  // Bit_Extender bit_extender_6
  assign bit_extender_7_out = {{31{inst[31]}}, inst[31]};  // Bit_Extender bit_extender_7
  assign bit_extender_8_out = {{24{1'b0}}, inst[19:12]};  // Bit_Extender bit_extender_8
  assign bit_extender_9_out = {{31{1'b0}}, inst[20]};  // Bit_Extender bit_extender_9
  // Probe on I
  Shifter #(.width(32)) shifter_1 (.in(bit_extender_2_out), .\dist (5'b00101), .out(shifter_1_out));
  Shifter #(.width(32)) shifter_2 (.in(bit_extender_4_out), .\dist (5'b00111), .out(shifter_2_out));
  Shifter #(.width(32)) shifter_3 (.in(bit_extender_5_out), .\dist (5'b00110), .out(shifter_3_out));
  assign bit_extender_10_out = {{26{1'b0}}, inst[30:25]};  // Bit_Extender bit_extender_10
  Shifter #(.width(32)) shifter_4 (.in(bit_extender_6_out), .\dist (5'b01100), .out(U));
  Shifter #(.width(32)) shifter_5 (.in(bit_extender_7_out), .\dist (5'b01111), .out(shifter_5_out));
  Shifter #(.width(32)) shifter_6 (.in(bit_extender_8_out), .\dist (5'b00111), .out(shifter_6_out));
  Shifter #(.width(32)) shifter_7 (.in(bit_extender_9_out), .\dist (5'b00110), .out(shifter_7_out));
  assign bit_extender_11_out = {{26{1'b0}}, inst[30:25]};  // Bit_Extender bit_extender_11
  Multiplexer #(.enable("false"), .select(3), .width(32)) multiplexer_1 (
    .in3(I), .in4(S), .in5(B), .in6(U), .in7(UJ), .out(imm), .sel(ImmSel));  // open: in0, in1, in2
  Adder #(.width(32)) adder_1 (.a(shifter_1_out), .b(bit_extender_3_out), .out(S));  // open: cin, cout
  Adder #(.width(32)) adder_2 (.a(shifter_2_out), .b(adder_3_out), .out(adder_2_out));  // open: cin, cout
  Adder #(.width(32)) adder_3 (.a(shifter_3_out), .b(bit_extender_10_out), .out(adder_3_out));  // open: cin, cout
  assign bit_extender_12_out = {{28{1'b0}}, inst[11:8]};  // Bit_Extender bit_extender_12
  // Probe on U
  Adder #(.width(32)) adder_4 (.a(shifter_7_out), .b(bit_extender_11_out), .out(adder_4_out));  // open: cin, cout
  // Probe on S
  Shifter #(.width(32)) shifter_8 (.in(adder_2_out), .\dist (5'b00101), .out(shifter_8_out));
  Shifter #(.width(32)) shifter_9 (.in(bit_extender_12_out), .\dist (5'b00001), .out(shifter_9_out));
  Adder #(.width(32)) adder_5 (.a(shifter_6_out), .b(adder_4_out), .out(adder_5_out));  // open: cin, cout
  Adder #(.width(32)) adder_6 (.a(shifter_8_out), .b(shifter_9_out), .out(B));  // open: cin, cout
  Adder #(.width(32)) adder_7 (.a(shifter_5_out), .b(adder_5_out), .out(adder_7_out));  // open: cin, cout
  // Probe on B
  // Probe on adder_7_out
  assign bit_extender_13_out = {{28{1'b0}}, inst[24:21]};  // Bit_Extender bit_extender_13
  Shifter #(.width(32)) shifter_10 (.in(adder_7_out), .\dist (5'b00101), .out(shifter_10_out));
  Shifter #(.width(32)) shifter_11 (.in(bit_extender_13_out), .\dist (5'b00001), .out(shifter_11_out));
  Adder #(.width(32)) adder_8 (.a(shifter_10_out), .b(shifter_11_out), .out(UJ));  // open: cin, cout
  // Probe on UJ

  // Notes on the sheet:
  //   INPUTS to your circuit
  //   DON'T CHANGE THE LOCATIONS OF THE INPUTS AND OUTPUTS!
  //   OUTPUT from your circuit
endmodule
