// Logisim project regfile.circ as structural Verilog: 1 circuit, main circuit regfile
module regfile (
  input  [4:0] rs1,
  input  [4:0] rs2,
  input  [4:0] rd,
  input  [31:0] Write_Data,
  input  RegWEn,
  input  clk,
  output [31:0] ra,
  output [31:0] sp,
  output [31:0] t0,
  output [31:0] t1,
  output [31:0] t2,
  output [31:0] s0,
  output [31:0] s1,
  output [31:0] a0,
  output [31:0] Read_Data_1,
  output [31:0] Read_Data_2
);

  wire x1W, x2W, x3W, x4W, x5W, x6W, x7W, x8W, x9W, x10W, x11W, x12W, x13W, x14W, x15W, x16W, x17W, x18W,
       x19W, x20W, x21W, x22W, x23W, x24W, x25W, x26W, x27W, x28W, x29W, x30W, x31W;
  wire [31:0] x0Q, x1D, x2D, x3D, x3Q, x4D, x4Q, x5D, x6D, x7D, x8D, x9D, x10D, x11D, x11Q, x12D, x12Q, x13D,
       x13Q, x14D, x14Q, x15D, x15Q, x16D, x16Q, x17D, x17Q, x18D, x18Q, x19D, x19Q, x20D, x20Q, x21D, x21Q,
       x22D, x22Q, x23D, x23Q, x24D, x24Q, x25D, x25Q, x26D, x26Q, x27D, x27Q, x28D, x28Q, x29D, x29Q, x30D,
       x30Q, x31D, x31Q;

  Register #(.width(32)) x0 (.en(1'b0), .clk(clk), .Q(x0Q));  // open: D, clr
  Register #(.width(32)) x8 (.D(x8D), .en(x8W), .clk(clk), .Q(s0));  // open: clr
  Register #(.width(32)) x16 (.D(x16D), .en(x16W), .clk(clk), .Q(x16Q));  // open: clr
  Register #(.width(32)) x24 (.D(x24D), .en(x24W), .clk(clk), .Q(x24Q));  // open: clr
  Register #(.width(32)) x1 (.D(x1D), .en(x1W), .clk(clk), .Q(ra));  // open: clr
  Register #(.width(32)) x9 (.D(x9D), .en(x9W), .clk(clk), .Q(s1));  // open: clr
  Register #(.width(32)) x17 (.D(x17D), .en(x17W), .clk(clk), .Q(x17Q));  // open: clr
  Register #(.width(32)) x25 (.D(x25D), .en(x25W), .clk(clk), .Q(x25Q));  // open: clr
  Multiplexer #(.enable("false"), .select(5), .width(32)) multiplexer_1 (
    .in0(x0Q), .in1(ra), .in2(sp), .in3(x3Q), .in4(x4Q), .in5(t0), .in6(t1), .in7(t2), .in8(s0), .in9(s1),
    .in10(a0), .in11(x11Q), .in12(x12Q), .in13(x13Q), .in14(x14Q), .in15(x15Q), .in16(x16Q), .in17(x17Q),
    .in18(x18Q), .in19(x19Q), .in20(x20Q), .in21(x21Q), .in22(x22Q), .in23(x23Q), .in24(x24Q), .in25(x25Q),
    .in26(x26Q), .in27(x27Q), .in28(x28Q), .in29(x29Q), .in30(x30Q), .in31(x31Q), .out(Read_Data_1), .sel(rs1));
  Register #(.width(32)) x2 (.D(x2D), .en(x2W), .clk(clk), .Q(sp));  // open: clr
  Register #(.width(32)) x10 (.D(x10D), .en(x10W), .clk(clk), .Q(a0));  // open: clr
  Register #(.width(32)) x18 (.D(x18D), .en(x18W), .clk(clk), .Q(x18Q));  // open: clr
  Register #(.width(32)) x26 (.D(x26D), .en(x26W), .clk(clk), .Q(x26Q));  // open: clr
  Register #(.width(32)) x3 (.D(x3D), .en(x3W), .clk(clk), .Q(x3Q));  // open: clr
  Register #(.width(32)) x11 (.D(x11D), .en(x11W), .clk(clk), .Q(x11Q));  // open: clr
  Register #(.width(32)) x19 (.D(x19D), .en(x19W), .clk(clk), .Q(x19Q));  // open: clr
  Register #(.width(32)) x27 (.D(x27D), .en(x27W), .clk(clk), .Q(x27Q));  // open: clr
  Multiplexer #(.enable("false"), .select(5), .width(32)) multiplexer_2 (
    .in0(x0Q), .in1(ra), .in2(sp), .in3(x3Q), .in4(x4Q), .in5(t0), .in6(t1), .in7(t2), .in8(s0), .in9(s1),
    .in10(a0), .in11(x11Q), .in12(x12Q), .in13(x13Q), .in14(x14Q), .in15(x15Q), .in16(x16Q), .in17(x17Q),
    .in18(x18Q), .in19(x19Q), .in20(x20Q), .in21(x21Q), .in22(x22Q), .in23(x23Q), .in24(x24Q), .in25(x25Q),
    .in26(x26Q), .in27(x27Q), .in28(x28Q), .in29(x29Q), .in30(x30Q), .in31(x31Q), .out(Read_Data_2), .sel(rs2));
  Register #(.width(32)) x4 (.D(x4D), .en(x4W), .clk(clk), .Q(x4Q));  // open: clr
  Register #(.width(32)) x12 (.D(x12D), .en(x12W), .clk(clk), .Q(x12Q));  // open: clr
  Register #(.width(32)) x20 (.D(x20D), .en(x20W), .clk(clk), .Q(x20Q));  // open: clr
  Register #(.width(32)) x28 (.D(x28D), .en(x28W), .clk(clk), .Q(x28Q));  // open: clr
  Demultiplexer #(.enable("false"), .select(5)) demultiplexer_1 (
    .out1(x1W), .out2(x2W), .out3(x3W), .out4(x4W), .out5(x5W), .out6(x6W), .out7(x7W), .out8(x8W),
    .out9(x9W), .out10(x10W), .out11(x11W), .out12(x12W), .out13(x13W), .out14(x14W), .out15(x15W),
    .out16(x16W), .out17(x17W), .out18(x18W), .out19(x19W), .out20(x20W), .out21(x21W), .out22(x22W),
    .out23(x23W), .out24(x24W), .out25(x25W), .out26(x26W), .out27(x27W), .out28(x28W), .out29(x29W),
    .out30(x30W), .out31(x31W), .in(RegWEn), .sel(rd));  // open: out0
  Register #(.width(32)) x5 (.D(x5D), .en(x5W), .clk(clk), .Q(t0));  // open: clr
  Register #(.width(32)) x13 (.D(x13D), .en(x13W), .clk(clk), .Q(x13Q));  // open: clr
  Register #(.width(32)) x21 (.D(x21D), .en(x21W), .clk(clk), .Q(x21Q));  // open: clr
  Register #(.width(32)) x29 (.D(x29D), .en(x29W), .clk(clk), .Q(x29Q));  // open: clr
  Register #(.width(32)) x6 (.D(x6D), .en(x6W), .clk(clk), .Q(t1));  // open: clr
  Register #(.width(32)) x14 (.D(x14D), .en(x14W), .clk(clk), .Q(x14Q));  // open: clr
  Register #(.width(32)) x22 (.D(x22D), .en(x22W), .clk(clk), .Q(x22Q));  // open: clr
  Register #(.width(32)) x30 (.D(x30D), .en(x30W), .clk(clk), .Q(x30Q));  // open: clr
  Demultiplexer #(.enable("false"), .select(5), .width(32)) demultiplexer_2 (
    .out1(x1D), .out2(x2D), .out3(x3D), .out4(x4D), .out5(x5D), .out6(x6D), .out7(x7D), .out8(x8D),
    .out9(x9D), .out10(x10D), .out11(x11D), .out12(x12D), .out13(x13D), .out14(x14D), .out15(x15D),
    .out16(x16D), .out17(x17D), .out18(x18D), .out19(x19D), .out20(x20D), .out21(x21D), .out22(x22D),
    .out23(x23D), .out24(x24D), .out25(x25D), .out26(x26D), .out27(x27D), .out28(x28D), .out29(x29D),
    .out30(x30D), .out31(x31D), .in(Write_Data), .sel(rd));  // open: out0
  Register #(.width(32)) x7 (.D(x7D), .en(x7W), .clk(clk), .Q(t2));  // open: clr
  Register #(.width(32)) x15 (.D(x15D), .en(x15W), .clk(clk), .Q(x15Q));  // open: clr
  Register #(.width(32)) x23 (.D(x23D), .en(x23W), .clk(clk), .Q(x23Q));  // open: clr
  Register #(.width(32)) x31 (.D(x31D), .en(x31W), .clk(clk), .Q(x31Q));  // open: clr

  // Other names for the same wires on the sheet: read_data1[31:0] = Read_Data_1; read_data2[31:0] = Read_Data_2;
  //   read_reg1[4:0] = rs1; read_reg2[4:0] = rs2; write_en = RegWEn; write_reg[4:0] = rd; x1Q[31:0] = ra;
  //   x2Q[31:0] = sp; x5Q[31:0] = t0; x6Q[31:0] = t1; x7Q[31:0] = t2; x8Q[31:0] = s0; x9Q[31:0] = s1; x10Q[31:0] = a0

  // Notes on the sheet:
  //   INPUTS to your circuit
  //   DON'T CHANGE THE LOCATIONS OF THE INPUTS AND OUTPUTS!
  //   These are DEBUG/TEST outputs from your circuit.
  //   OUTPUTS from your circuit
endmodule
